# Fritzing sketch tube-radio-FM (saved by Fritzing 0.9.2b)

parts:
  ProMini_3_3V = Arduino Pro Mini v13
  1K = Resistor [tolerance=±5% resistance=220 package=THT]
  1K_2 = Resistor [tolerance=±5% resistance=220 package=THT]
  NE555 = General purpose bipolar Timer [package=dil-08]
  1M = Resistor [tolerance=±5% resistance=220 package=THT]
  1M_2 = Resistor [tolerance=±5% resistance=220 package=THT]
  RDA5807M_RRD102 = DIP - 10 pins [chip_label=IC package="DIP (Dual Inline) [THT]"]

nets:
  N1: ProMini_3_3V.A4, RDA5807M_RRD102.DATA
  N2: ProMini_3_3V.A5, RDA5807M_RRD102.SCLK
  GND: ProMini_3_3V.GND, NE555.GND, RDA5807M_RRD102.GND
  VCC: ProMini_3_3V.VCC, NE555._RES, NE555.VCC+, 1M.Pin_1, RDA5807M_RRD102.VCC
  N3: ProMini_3_3V.D5_PWM, NE555.OUT
  N4: 1K.Pin_0, 1K_2.Pin_0
  N5: 1K.Pin_1, RDA5807M_RRD102.LOUT
  N6: 1K_2.Pin_1, RDA5807M_RRD102.ROUT
  N7: NE555.TRI, NE555.TRE, 1M_2.Pin_1
  N8: NE555.DIS, 1M.Pin_0, 1M_2.Pin_0

notes:
  3.3 to 9V DC
  pick up
  amp input
  Variable Capacitor

custom parts:
  DIP - 10 pins: A DIP stand-in part for whatever IC you want. With 10 pins on a 300mil dual inline package (DIP) footprint.
